// Logisim project Processador.circ as structural Verilog: 2 circuits, main circuit main
module main (
  output [7:0] out_1
);

  wire Clk;
  wire [7:0] adder_1_out, PC_q;

  Register PC (.D(adder_1_out), .en(1'b1), .clk(Clk), .Q(PC_q));  // open: clr
  Clock clock_1 (.out(Clk));
  Adder adder_1 (.a(PC_q), .b(8'h1), .out(adder_1_out));  // open: cin, cout
  ROM rom_1 (.addr(PC_q), .data(out_1));
  BancoDeRegistradores bancoderegistradores_1 ();  // open: rs1, rs2, rd
endmodule

module BancoDeRegistradores (
  input  rs1,
  input  rs2,
  input  rd
);

  Clock clock_1 ();  // open: out
  Demultiplexer demultiplexer_1 ();  // open: out0, out1, in, sel
  Register #(.width(4)) OP ();  // open: D, en, clk, Q, clr
  Register #(.width(20)) rd_rs1 ();  // open: D, en, clk, Q, clr
  Register #(.width(20)) register_1 ();  // open: D, en, clk, Q, clr
  Register #(.width(20)) register_2 ();  // open: D, en, clk, Q, clr
  Multiplexer multiplexer_1 ();  // open: in0, in1, out, sel
endmodule
